# Fritzing sketch steppers (saved by Fritzing 0.9.3b)

parts:
  Componente1 = Arduino Uno (Rev3)
  Driver1 = 28BYJ-48 Driver Module [part_number=ULN2003 package=THT]
  SM1 = 28BYJ-48 Stepper Motor [part_number=28BYJ-48]
  Driver2 = 28BYJ-48 Driver Module [part_number=ULN2003 package=THT]
  SM2 = 28BYJ-48 Stepper Motor [part_number=28BYJ-48]  # not connected

nets:
  N1: Componente1.D8, Driver2.IN2
  N2: Componente1.D9_PWM, Driver2.IN1
  N3: Componente1.D2, Driver1.IN1
  N4: Componente1.D3_PWM, Driver1.IN2
  N5: Componente1.D4, Driver1.IN3
  N6: Componente1.D5_PWM, Driver1.IN4
  N7: Componente1.D6_PWM, Driver2.IN4
  N8: Componente1.D7, Driver2.IN3
  N9: Driver1.blue-pin, SM1.blue-pin
  N10: Driver1.pink-pin, SM1.pink-pin
  N11: Driver1.yellow-pin, SM1.yellow-pin
  N12: Driver1.orange-pin, SM1.orange-pin
  N13: Driver1.red-pin, SM1.red-pin

notes:
  Stepper derecho
  Stepper izquierdo

custom parts:
  28BYJ-48 Driver Module: ULN2003 Driver Module for the 28BYJ-48 Unipolar Stepper Motor LED A - Blue wire - Bottom coil left LED B - Pink wire - Top coil left LED C - Yellow wire - Bottom coil right LED D - Orange wire - Top coil right Common rail - red Connector pins: blue - pink - yellow - orange - red Control pins - IN1 to IN4 Power pins - GND & Vmotor (5-12V) On/Off jumper (if removed, power to motor is cut).
  28BYJ-48 Stepper Motor: Unipolar Stepper Motor 28BYJ-48 Top coil - pink & orange Bottom coil - blue & yellow Common rail - red Connector pins: blue - pink - yellow - orange - red
